// Logisim project game.circ as structural Verilog: 6 circuits, main circuit main
module main (
);

  wire _1_out, _2_out, and_2_out, and_4_out, and_5_out, and_6_out, and_8_out, and_9_out, and_10_out,
       arbiter_1_iack_2, arbiter_1_vec, arbiter_2_iack_2, arbiter_2_ireq_2, arbiter_2_vec, arbiter_3_ireq_2,
       arbiter_3_vec, bank0, bank1, bank2, cdm_8_mark5_1_data_inst, cdm_8_mark5_1_mem_cycle, clk,
       comparator_1_eq, comparator_2_eq, comparator_3_eq, data, decoder_1_out0, decoder_4_out1, GameOver,
       gsdd_1_draw, gsdd_1_o_win, gsdd_1_x_win, hclock, I_4, I_Osel, IAck, In_Out, \input , input_flag,
       input_players, IO_3_out, IO_4_out, IRQ, NextGame, not_1_out, not_2_out, not_3_out, or_1_out, or_2_out,
       pull_resistor_1_node, reset_all, reset_flag, ResetBtn, shift1, shift2, st_4, transistor_1_out, \wait ,
       X_2_out, X_3_out, X_4_out, X_5_out, X_6_out, X_7_out, X_8_out, X_9_out, X_out;
  wire [1:0] controlled_buffer_1_out, GS, sdr_1_h0, sdr_1_h1, sdr_1_h2, sdr_1_v2;
  wire [2:0] vec;
  wire [2:2] tttc_1_hout, tttc_2_hout, tttc_3_hout;
  wire [3:0] bpc_1_p9, controlled_buffer_1_out_2, gsdd_1_o_score, gsdd_1_x_score, I_Oadr;
  wire [4:0] sdr_1_v1, tttc_1_l0, tttc_1_l1, tttc_1_l2, tttc_1_l3, tttc_1_l4, tttc_2_l0, tttc_2_l1,
       tttc_2_l2, tttc_2_l3, tttc_2_l4, tttc_3_l0, tttc_3_l1, tttc_3_l2, tttc_3_l3, tttc_3_l4, tttc_4_l0,
       tttc_4_l1, tttc_4_l2, tttc_4_l3, tttc_4_l4, tttc_5_l0, tttc_5_l1, tttc_5_l2, tttc_5_l3, tttc_5_l4,
       tttc_6_l0, tttc_6_l1, tttc_6_l2, tttc_6_l3, tttc_6_l4, tttc_7_l0, tttc_7_l1, tttc_7_l2, tttc_7_l3,
       tttc_7_l4, tttc_8_l0, tttc_8_l1, tttc_8_l2, tttc_8_l3, tttc_8_l4, tttc_9_l0, tttc_9_l1, tttc_9_l2,
       tttc_9_l3, tttc_9_l4;
  wire [4:2] sdr_1_v2_2;
  wire [5:0] sdr_1_v0;
  wire [5:5] tttc_4_vout, tttc_7_vout;
  wire [7:0] cdm_8_mark5_1_data_out, controlled_buffer_2_out, I_Odat, PC, players;
  wire [7:4] cdm_8_mark5_1_addr;

  Clock clock_1 (.out(clk));
  Button R (.out(ResetBtn));
  Comparator #(.mode("unsigned")) comparator_1 (.a(PC), .b(8'hf8), .eq(comparator_1_eq));  // open: gt, lt
  Comparator #(.mode("unsigned")) comparator_2 (.a(PC), .b(8'hf6), .eq(comparator_2_eq));  // open: gt, lt
  assign {GS, controlled_buffer_1_out_2, controlled_buffer_1_out} = hclock ? I_Odat : 8'bz;  // Controlled_Buffer controlled_buffer_1
  T_Flip_Flop t_ff_1 (.clk(comparator_1_eq), .T(1'b1), .Q(shift1), .reset(reset_all));  // open: Qn, preset, en
  T_Flip_Flop t_ff_2 (.clk(comparator_2_eq), .T(1'b1), .Q(shift2), .reset(reset_all));  // open: Qn, preset, en
  Decoder #(.disabled(0)) decoder_1 (
    .out0(decoder_1_out0), .out1(data), .sel(cdm_8_mark5_1_data_inst), .en(cdm_8_mark5_1_mem_cycle));
  CdM_8_mark5 cdm_8_mark5_1 (
    .clock(clk), .addr({cdm_8_mark5_1_addr, I_Oadr}), .mem_read(In_Out), .mem_cycle(cdm_8_mark5_1_mem_cycle),
    .data_inst(cdm_8_mark5_1_data_inst), .data_out(cdm_8_mark5_1_data_out),
    .data_in(controlled_buffer_2_out), .PC(PC), .IAck(IAck), .IRQ(IRQ), .vec(vec));  // open: r0, r1, r2, r3, SP, PS
  not not_1 (not_1_out, In_Out);
  assign controlled_buffer_2_out = In_Out ? I_Odat : 8'bz;  // Controlled_Buffer controlled_buffer_2
  SDR sdr_1 (
    .XY(controlled_buffer_1_out_2), .symID(controlled_buffer_1_out), .H0(sdr_1_h0), .H1(sdr_1_h1),
    .H2(sdr_1_h2), .V0(sdr_1_v0[4:0]), .V1(sdr_1_v1), .V2({sdr_1_v2_2, sdr_1_v2}), .clock(hclock),
    .Input(\input ), .reset_all(reset_all), .\wait (input_flag), .st_4(st_4));
  and and_1 (I_Osel, ~cdm_8_mark5_1_addr[4], cdm_8_mark5_1_addr[5], cdm_8_mark5_1_addr[6], cdm_8_mark5_1_addr[7], data);  // AND_Gate
  Decoder #(.select(2), .disabled(0)) decoder_2 (
    .out0(bank0), .out1(bank1), .out2(bank2), .sel({shift2, shift1}), .en(decoder_1_out0));  // open: out3
  assign I_Odat = not_1_out ? cdm_8_mark5_1_data_out : 8'bz;  // Controlled_Buffer controlled_buffer_3
  and IO_3 (IO_3_out, I_Osel, I_Oadr[0], I_Oadr[1], ~I_Oadr[2], ~I_Oadr[3]);  // AND_Gate
  Decoder #(.disabled(0)) decoder_3 (.out0(hclock), .out1(reset_flag), .sel(In_Out), .en(IO_3_out));
  DotMatrix #(.inputtype("row"), .matrixrows(5)) dotmatrix_1 (
    .row0(tttc_1_l0), .row1(tttc_1_l1), .row2(tttc_1_l2), .row3(tttc_1_l3), .row4(tttc_1_l4));
  TTTC tttc_1 (
    .hin(sdr_1_h0), .vin(sdr_1_v0[1:0]), .btn(X_out), .L0(tttc_1_l0), .L1(tttc_1_l1), .L2(tttc_1_l2),
    .L3(tttc_1_l3), .hout(tttc_1_hout[2]), .vout(sdr_1_v0[5]), .reset_all(sdr_1_v0[4]), .L4(tttc_1_l4),
    .\wait (sdr_1_v0[2]), .st_4(sdr_1_v0[3]));
  Button X (.out(X_out));
  DotMatrix #(.inputtype("row"), .matrixrows(5)) dotmatrix_2 (
    .row0(tttc_2_l0), .row1(tttc_2_l1), .row2(tttc_2_l2), .row3(tttc_2_l3), .row4(tttc_2_l4));
  TTTC tttc_2 (
    .hin(sdr_1_h1), .vin(sdr_1_v0[1:0]), .btn(X_2_out), .L0(tttc_2_l0), .L1(tttc_2_l1), .L2(tttc_2_l2),
    .L3(tttc_2_l3), .hout(tttc_2_hout[2]), .vout(sdr_1_v0[5]), .reset_all(sdr_1_v0[4]), .L4(tttc_2_l4),
    .\wait (sdr_1_v0[2]), .st_4(sdr_1_v0[3]));
  Button X_2 (.out(X_2_out));
  DotMatrix #(.inputtype("row"), .matrixrows(5)) dotmatrix_3 (
    .row0(tttc_3_l0), .row1(tttc_3_l1), .row2(tttc_3_l2), .row3(tttc_3_l3), .row4(tttc_3_l4));
  TTTC tttc_3 (
    .hin(sdr_1_h2), .vin(sdr_1_v0[1:0]), .btn(X_3_out), .L0(tttc_3_l0), .L1(tttc_3_l1), .L2(tttc_3_l2),
    .L3(tttc_3_l3), .hout(tttc_3_hout[2]), .vout(sdr_1_v0[5]), .reset_all(sdr_1_v0[4]), .L4(tttc_3_l4),
    .\wait (sdr_1_v0[2]), .st_4(sdr_1_v0[3]));
  Button X_3 (.out(X_3_out));
  // Probe on {cdm_8_mark5_1_addr, I_Oadr}
  and and_2 (and_2_out, data, ~I_Osel);  // AND_Gate
  // Probe on I_Odat
  RAM ram_1 (
    .addr({cdm_8_mark5_1_addr, I_Oadr}), .data(I_Odat), .sel(and_2_out), .clk(clk), .ld(In_Out),
    .clr(reset_all));
  ROM rom_1 (.addr({cdm_8_mark5_1_addr, I_Oadr}), .data(I_Odat), .sel(bank0));
  ROM rom_2 (.addr({cdm_8_mark5_1_addr, I_Oadr}), .data(I_Odat), .sel(bank1));
  ROM rom_3 (.addr({cdm_8_mark5_1_addr, I_Oadr}), .data(I_Odat), .sel(bank2));
  DotMatrix #(.inputtype("row"), .matrixrows(5)) dotmatrix_4 (
    .row0(tttc_4_l0), .row1(tttc_4_l1), .row2(tttc_4_l2), .row3(tttc_4_l3), .row4(tttc_4_l4));
  TTTC tttc_4 (
    .hin(sdr_1_h0), .vin(sdr_1_v1[1:0]), .btn(X_4_out), .L0(tttc_4_l0), .L1(tttc_4_l1), .L2(tttc_4_l2),
    .L3(tttc_4_l3), .hout(tttc_1_hout[2]), .vout(tttc_4_vout[5]), .reset_all(sdr_1_v1[4]), .L4(tttc_4_l4),
    .\wait (sdr_1_v1[2]), .st_4(sdr_1_v1[3]));
  Button X_4 (.out(X_4_out));
  DotMatrix #(.inputtype("row"), .matrixrows(5)) dotmatrix_5 (
    .row0(tttc_5_l0), .row1(tttc_5_l1), .row2(tttc_5_l2), .row3(tttc_5_l3), .row4(tttc_5_l4));
  TTTC tttc_5 (
    .hin(sdr_1_h1), .vin(sdr_1_v1[1:0]), .btn(X_5_out), .L0(tttc_5_l0), .L1(tttc_5_l1), .L2(tttc_5_l2),
    .L3(tttc_5_l3), .hout(tttc_2_hout[2]), .vout(tttc_4_vout[5]), .reset_all(sdr_1_v1[4]), .L4(tttc_5_l4),
    .\wait (sdr_1_v1[2]), .st_4(sdr_1_v1[3]));
  Button X_5 (.out(X_5_out));
  DotMatrix #(.inputtype("row"), .matrixrows(5)) dotmatrix_6 (
    .row0(tttc_6_l0), .row1(tttc_6_l1), .row2(tttc_6_l2), .row3(tttc_6_l3), .row4(tttc_6_l4));
  TTTC tttc_6 (
    .hin(sdr_1_h2), .vin(sdr_1_v1[1:0]), .btn(X_6_out), .L0(tttc_6_l0), .L1(tttc_6_l1), .L2(tttc_6_l2),
    .L3(tttc_6_l3), .hout(tttc_3_hout[2]), .vout(tttc_4_vout[5]), .reset_all(sdr_1_v1[4]), .L4(tttc_6_l4),
    .\wait (sdr_1_v1[2]), .st_4(sdr_1_v1[3]));
  Button X_6 (.out(X_6_out));
  and and_3 (reset_all, pull_resistor_1_node, not_2_out);
  not not_2 (not_2_out, pull_resistor_1_node);
  Pull_Resistor pull_resistor_1 (.node(pull_resistor_1_node));
  buf buffer_1 (pull_resistor_1_node, vec[1]);
  Comparator #(.mode("unsigned")) comparator_3 (.a(I_Odat), .b(8'hd5), .eq(comparator_3_eq));  // open: gt, lt
  and and_4 (and_4_out, ~IRQ, ~IAck);  // AND_Gate
  Transistor #(.\type ("n")) transistor_1 (.in(comparator_3_eq), .out(transistor_1_out), .gate(In_Out));
  not not_3 (not_3_out, transistor_1_out);
  DotMatrix #(.inputtype("row"), .matrixrows(5)) dotmatrix_7 (
    .row0(tttc_7_l0), .row1(tttc_7_l1), .row2(tttc_7_l2), .row3(tttc_7_l3), .row4(tttc_7_l4));
  TTTC tttc_7 (
    .hin(sdr_1_h0), .vin(sdr_1_v2), .btn(X_7_out), .L0(tttc_7_l0), .L1(tttc_7_l1), .L2(tttc_7_l2),
    .L3(tttc_7_l3), .hout(tttc_1_hout[2]), .vout(tttc_7_vout[5]), .reset_all(sdr_1_v2_2[4]), .L4(tttc_7_l4),
    .\wait (sdr_1_v2_2[2]), .st_4(sdr_1_v2_2[3]));
  Button X_7 (.out(X_7_out));
  DotMatrix #(.inputtype("row"), .matrixrows(5)) dotmatrix_8 (
    .row0(tttc_8_l0), .row1(tttc_8_l1), .row2(tttc_8_l2), .row3(tttc_8_l3), .row4(tttc_8_l4));
  TTTC tttc_8 (
    .hin(sdr_1_h1), .vin(sdr_1_v2), .btn(X_8_out), .L0(tttc_8_l0), .L1(tttc_8_l1), .L2(tttc_8_l2),
    .L3(tttc_8_l3), .hout(tttc_2_hout[2]), .vout(tttc_7_vout[5]), .reset_all(sdr_1_v2_2[4]), .L4(tttc_8_l4),
    .\wait (sdr_1_v2_2[2]), .st_4(sdr_1_v2_2[3]));
  Button X_8 (.out(X_8_out));
  DotMatrix #(.inputtype("row"), .matrixrows(5)) dotmatrix_9 (
    .row0(tttc_9_l0), .row1(tttc_9_l1), .row2(tttc_9_l2), .row3(tttc_9_l3), .row4(tttc_9_l4));
  TTTC tttc_9 (
    .hin(sdr_1_h2), .vin(sdr_1_v2), .btn(X_9_out), .L0(tttc_9_l0), .L1(tttc_9_l1), .L2(tttc_9_l2),
    .L3(tttc_9_l3), .hout(tttc_3_hout[2]), .vout(tttc_7_vout[5]), .reset_all(sdr_1_v2_2[4]), .L4(tttc_9_l4),
    .\wait (sdr_1_v2_2[2]), .st_4(sdr_1_v2_2[3]));
  Button X_9 (.out(X_9_out));
  assign vec = arbiter_1_vec ? 3'b001 : 3'bz;  // Controlled_Buffer controlled_buffer_4
  S_R_Flip_Flop #(.trigger("low")) s_r_ff_1 (
    .S(I_4), .clk(1'b0), .R(reset_flag), .Q(st_4), .reset(reset_all));  // open: Qn, preset, en
  S_R_Flip_Flop #(.trigger("high")) s_r_ff_2 (
    .S(transistor_1_out), .clk(clk), .R(not_3_out), .Q(\wait ), .reset(reset_all));  // open: Qn, preset, en
  Decoder #(.disabled(0)) decoder_4 (.out0(I_4), .out1(decoder_4_out1), .sel(In_Out), .en(IO_4_out));
  and IO_4 (IO_4_out, I_Osel, ~I_Oadr[0], ~I_Oadr[1], I_Oadr[2], ~I_Oadr[3]);  // AND_Gate
  arbiter arbiter_1 (
    .IReq_2(IRQ), .IAck(IAck), .IReq(arbiter_2_ireq_2), .IAck_2(arbiter_1_iack_2), .vec(arbiter_1_vec),
    .req(and_5_out), .done(and_4_out), .clock(clk));
  and and_5 (and_5_out, \input , input_flag);
  assign vec = arbiter_2_vec ? 3'b000 : 3'bz;  // Controlled_Buffer controlled_buffer_5
  arbiter arbiter_2 (
    .IReq_2(arbiter_2_ireq_2), .IAck(arbiter_1_iack_2), .IReq(arbiter_3_ireq_2), .IAck_2(arbiter_2_iack_2),
    .vec(arbiter_2_vec), .req(and_6_out), .done(and_4_out), .clock(clk));
  and and_6 (and_6_out, \wait , input_players);
  or or_1 (or_1_out, players[0], players[1]);
  assign I_Odat = reset_flag ? {\input , 3'b000, bpc_1_p9} : 8'bz;  // Controlled_Buffer controlled_buffer_6
  // BPC bpc_1: pin names not known; wires that end beside it: tttc_1_hout[2], tttc_2_hout[2], tttc_3_hout[2], reset_flag, \input , tttc_7_vout[5], tttc_4_vout[5], sdr_1_v0[5], bpc_1_p9, reset_all
  assign vec = arbiter_3_vec ? 3'b010 : 3'bz;  // Controlled_Buffer controlled_buffer_7
  arbiter arbiter_3 (
    .IReq_2(arbiter_3_ireq_2), .IAck(arbiter_2_iack_2), .IReq(1'b0), .vec(arbiter_3_vec), .req(or_2_out),
    .done(and_4_out), .clock(clk));  // open: IAck_2
  or or_2 (or_2_out, ResetBtn, and_9_out);
  and and_7 (input_flag, \wait , or_1_out, ~GameOver, ~IRQ, ~IAck);  // AND_Gate
  assign I_Odat = decoder_4_out1 ? players : 8'bz;  // Controlled_Buffer controlled_buffer_8
  Button _1 (.out(_1_out));
  Hex_Digit_Display hex_digit_display_1 (.value(gsdd_1_o_score));  // open: dp
  LED led_1 (.in(gsdd_1_o_win));
  GSDD gsdd_1 (
    .score(GS), .O_win(gsdd_1_o_win), .X_win(gsdd_1_x_win), .draw(gsdd_1_draw), .clock(hclock),
    .reset_all(reset_all), .O_score(gsdd_1_o_score), .X_score(gsdd_1_x_score), .NextGame(NextGame),
    .GameOver(GameOver));
  LED led_2 (.in(and_8_out));
  and and_8 (and_8_out, st_4, input_flag);
  and and_9 (and_9_out, GameOver, NextGame);
  CofP cofp_1 (
    ._1_player(_1_out), ._2_players(_2_out), .count_of_players(players), .\wait (\wait ),
    .reset_all(reset_all), .input_players(input_players), .reset(decoder_4_out1), .ResetBtn(ResetBtn));
  Button _2 (.out(_2_out));
  Hex_Digit_Display hex_digit_display_2 (.value(gsdd_1_x_score));  // open: dp
  LED led_3 (.in(gsdd_1_draw));
  LED led_4 (.in(gsdd_1_x_win));
  Button N (.out(NextGame));
  LED led_5 (.in(and_10_out));
  and and_10 (and_10_out, input_flag, ~st_4);  // AND_Gate

  // Notes on the sheet:
  //   Reset
  //   contents of rom_1 (hex, n*v repeats v):
  //   d0 0 c1 d1 8 a4 c5 cd 0 d0 10 c0 d0 80 c0 d9 d0 e4 b1 5 e1 19 d5 ee 20 d0 2 74 e1 20 ee f6 d6 83 c2
  //   d6 41 c6 d1 c0 4d 5 e1 30 ee f8 ee 3e d1 c0 77 e0 39 d6 90 ee 3e d1 e3 d3 ff a7 ee 20 d4 d0 a7 d3 8
  //   f ed 68 8b f1 8c b5 5 ed 64 6 f1 b5 8c 79 e1 61 f1 b5 8c 79 e1 5f d3 80 d7 ee 62 8c ee 66 8c 8c ee
  //   45 30 d2 3 d1 a 74 eb 80 b3 f e1 77 d3 0 d7 8c 78 e1 7e 8c d2 7 ee 6d d3 c0 d7 d5 c4 c4 d0 e3 b2 d1
  //   f 49 d3 2 a7 d7 d2 3 32 d1 3 5 ed a6 3f fb 2f 2f d0 83 5c d3 e3 ac 8e 89 ee 95 d7 0 1 2 4 5 6 8 9 a
  //   0 4 8 1 5 9 2 6 a 0 5 a 8 5 2 49*0 10 80 84 80 4*0 ee 20
  //   contents of rom_2 (hex, n*v repeats v):
  //   d3 2 d6 25 f eb 1b d3 1 d6 25 f eb 15 d6 79 f eb 15 d6 90 d2 1 d6 9c ee 23 c2 d2 41 d6 9c c6 d6 a4
  //   ee f8 d0 c8 d2 8 a ed 62 8a c2 3a f1 b5 8c 7d e0 5d 5 e1 39 8e f1 b5 8c 7d e0 5a 5 e1 43 8e f1 b5 8c
  //   7d e0 58 5 e1 4d 8e d1 1 79 e1 58 d6 63 c7 d3 ff d7 ee 5b 8c ee 5f 8c 8c c6 ee 29 d7 3a 88 88 88 f1
  //   b5 5 e0 72 8c f1 b5 8e ee 69 c2 f1 d2 1 a6 c6 d7 d0 5 b1 5 e1 84 d1 1 a1 d3 ff 1 d7 b4 0 e1 8f d0 1
  //   a4 d3 ff d7 d2 c0 f eb 9b f9 d6 86 8e ee 92 d7 7 97 97 5b d2 e3 ab d7 a ed ab 88 8a ee a4 d1 3 2 5
  //   ed bf 3f fb 97 97 d0 43 5c d3 e3 ac 8e 89 ee ae d7 8 a 2 0 1 4 6 9 0 1 2 4 5 6 8 9 a 0 4 8 1 5 9 2 6
  //   a 0 5 a 8 5 2 24*0 ee
  //   contents of rom_3 (hex, n*v repeats v):
  //   d3 2 d6 5b c2 d6 82 c6 d1 80 4d 5 e1 3b d3 e4 af d3 1 d6 5b c2 d6 82 c6 d1 80 4d 5 e1 23 ee 0 ee 39
  //   d1 40 4d 5 e1 39 d3 40 d1 f 49 d2 1 d6 66 88 88 88 d3 40 d6 6e ee 58 d1 40 4d 5 e1 51 d1 f 49 d2 2
  //   d6 66 88 88 88 d3 80 d6 6e ee 58 d1 f 49 d2 2 d6 66 ee 0 d4 d5 c4 c4 d0 e3 b2 d1 f 49 a7 d7 25 25 56
  //   5b d2 e3 ab d7 d1 3 5 ed 81 c1 f1 d2 c0 4b d2 3 d6 66 8c c5 89 ee 70 d7 d0 c4 d3 8 f ed a9 8b f1 8c
  //   b5 5 ed a5 6 f1 b5 8c 79 e1 a2 f1 b5 8c 79 e1 a0 d3 80 d7 ee a3 8c ee a7 8c 8c ee 86 30 d2 3 d1 a 74
  //   eb c1 b3 f e1 b8 d3 0 d7 8c 78 e1 bf 8c d2 7 ee ae d3 c0 d7 0 1 2 4 5 6 8 9 a 0 4 8 1 5 9 2 6 a 0 5
  //   a 8 5 2 22*0 5c 80 0 0 ee
  //   O turn
  //   O    |    X
  //   Continue
  //   X turn
endmodule

module TTTC (
  input  [1:0] hin,
  input  [1:0] vin,
  input  reset_all,
  input  btn,
  input  \wait ,
  input  st_4,
  output [4:0] L0,
  output [4:0] L1,
  output [4:0] L2,
  output [4:0] L3,
  output [4:0] L4,
  output hout,
  output vout
);

  wire and_1_out, and_2_out, xor_1_out;
  wire [1:0] multiplexer_1_out, multiplexer_2_out, sym_reg_q;

  Pull_Resistor pull_resistor_1 (.node(hin[0]));
  Pull_Resistor pull_resistor_2 (.node(hin[1]));
  Pull_Resistor pull_resistor_3 (.node(vin[0]));
  and and_1 (and_1_out, hin[1], vin[1]);
  Pull_Resistor pull_resistor_4 (.node(vin[1]));
  Multiplexer #(.width(2), .disabled(0), .enable("false")) multiplexer_1 (
    .in0(2'b10), .in1(2'b01), .out(multiplexer_1_out), .sel(st_4));
  // Probe on multiplexer_2_out
  Multiplexer #(.width(2), .disabled(0), .enable("false")) multiplexer_2 (
    .in0({vin[0], hin[0]}), .in1(multiplexer_1_out), .out(multiplexer_2_out), .sel(and_2_out));
  Register #(.width(2), .trigger("high")) sym_reg (
    .D(multiplexer_2_out), .Q(sym_reg_q), .clk(xor_1_out), .clr(reset_all));  // open: en
  xor xor_1 (xor_1_out, and_1_out, and_2_out);
  Transistor #(.\type ("n")) transistor_1 (.in(1'b0), .out(hout), .gate(and_2_out));
  and and_2 (and_2_out, ~sym_reg_q[0], ~sym_reg_q[1], btn, \wait );  // AND_Gate
  ROM #(.addrWidth(2), .dataWidth(25)) rom_1 (.addr(sym_reg_q), .data({L4, L3, L2, L1, L0}));  // open: sel

  assign vout = hout;

  // Notes on the sheet:
  //   symID
  //   contents of rom_1 (hex, n*v repeats v):
  //   0 e8c62e 1151151 1ffffff
endmodule

module SDR (
  input  [3:0] XY,
  input  clock,
  input  [1:0] symID,
  input  Input,
  input  reset_all,
  input  \wait ,
  input  st_4,
  output [1:0] H0,
  output [1:0] H1,
  output [1:0] H2,
  output [4:0] V0,
  output [4:0] V1,
  output [4:0] V2
);

  Demultiplexer #(.select(2), .width(2), .tristate("true"), .enable("false")) demultiplexer_1 (
    .out0(H0), .out1(H1), .out2(H2), .in({clock, symID[0]}), .sel(XY[3:2]));  // open: out3
  Demultiplexer #(.select(2), .width(2), .tristate("true"), .enable("false")) demultiplexer_2 (
    .out0(V0[1:0]), .out1(V1[1:0]), .out2(V2[1:0]), .in({clock, symID[1]}), .sel(XY[1:0]));  // open: out3
  and and_1 (V0[2], ~Input, \wait );  // AND_Gate
  and and_2 (V1[2], ~Input, \wait );  // AND_Gate
  and and_3 (V2[2], ~Input, \wait );  // AND_Gate

  assign V0[4:3] = {reset_all, st_4};
  assign V1[4:3] = {reset_all, st_4};
  assign V2[4:3] = {reset_all, st_4};
endmodule

module BPC (
  input  H2,
  input  H1,
  input  H0,
  input  V2,
  input  V1,
  input  V0,
  input  reset,
  input  reset_all,
  output [3:0] XY,
  output \input 
);

  wire and_1_out, and_2_out, nand_1_out, not_1_out, not_2_out, not_3_out;

  buf buffer_1 (H1, H0);
  Pull_Resistor #(.pull(1)) pull_resistor_1 (.node(H1));
  Pull_Resistor #(.pull(1)) pull_resistor_2 (.node(H2));
  buf buffer_2 (H2, H0);
  buf buffer_3 (V1, V0);
  Pull_Resistor #(.pull(1)) pull_resistor_3 (.node(V1));
  buf buffer_4 (V2, V0);
  Pull_Resistor #(.pull(1)) pull_resistor_4 (.node(V2));
  not not_1 (not_1_out, reset);
  not not_2 (not_2_out, not_1_out);
  nand nand_1 (nand_1_out, H1, H2, V1, V2);
  not not_3 (not_3_out, nand_1_out);
  and and_1 (and_1_out, nand_1_out, not_3_out);
  and and_2 (and_2_out, not_1_out, not_2_out);
  S_R_Flip_Flop #(.trigger("low")) s_r_ff_1 (
    .S(and_1_out), .clk(1'b0), .R(and_2_out), .Q(\input ), .reset(reset_all));  // open: Qn, preset, en
  Register #(.width(4)) XY_reg (.D({V1, V2, H1, H2}), .Q(XY), .clk(nand_1_out), .clr(reset_all));  // open: en
endmodule

module GSDD (
  input  [1:0] score,
  input  clock,
  input  reset_all,
  input  NextGame,
  output [3:0] O_score,
  output O_win,
  output GameOver,
  output X_win,
  output [3:0] X_score,
  output draw
);

  wire d_ff_1_q, or_1_out, or_2_out, transistor_1_out, transistor_2_out;
  wire [1:0] register_1_q;

  Register #(.width(2), .trigger("high")) register_1 (
    .D(score), .Q(register_1_q), .clk(clock), .clr(reset_all));  // open: en
  Transistor #(.\type ("n")) transistor_1 (.in(NextGame), .out(transistor_1_out), .gate(GameOver));
  Decoder #(.select(2), .enable("false")) decoder_1 (
    .out1(O_win), .out2(X_win), .out3(draw), .sel(register_1_q));  // open: out0
  D_Flip_Flop d_ff_1 (.clk(transistor_1_out), .D(1'b1), .Q(d_ff_1_q), .reset(reset_all));  // open: Qn, preset, en
  Transistor #(.gate("br")) transistor_2 (.in(reset_all), .out(transistor_2_out), .gate(d_ff_1_q));
  or or_1 (or_1_out, O_win, draw);
  or or_2 (or_2_out, X_win, draw);
  or or_3 (GameOver, or_1_out, or_2_out);
  Counter #(.width(4), .max('h9), .ongoal("stay")) counter_1 (
    .count(1'b1), .Q(O_score), .clk(or_1_out), .clr(transistor_2_out));  // open: load, D, carry
  Counter #(.width(4), .max('h9), .ongoal("stay")) counter_2 (
    .count(1'b1), .Q(X_score), .clk(or_2_out), .clr(transistor_2_out));  // open: load, D, carry
endmodule

module CofP (
  input  _1_player,
  input  _2_players,
  input  reset_all,
  input  \wait ,
  input  ResetBtn,
  input  reset,
  output [7:0] count_of_players,
  output input_players
);

  wire and_1_out, and_2_out, and_3_out, d_ff_1_q, not_1_out, not_2_out, not_3_out, not_4_out,
       transistor_1_out;

  Transistor #(.\type ("n"), .gate("br")) transistor_1 (.in(reset_all), .out(transistor_1_out), .gate(d_ff_1_q));
  D_Flip_Flop d_ff_1 (.clk(ResetBtn), .D(1'b1), .Q(d_ff_1_q), .reset(reset_all));  // open: Qn, preset, en
  not not_1 (not_1_out, reset);
  and and_1 (and_1_out, not_1_out, not_2_out);
  not not_2 (not_2_out, not_1_out);
  Register #(.width(2), .trigger("high")) register_1 (
    .D({_2_players, _1_player}), .en(and_2_out), .Q(count_of_players[1:0]), .clk(\wait ),
    .clr(transistor_1_out));
  and and_2 (and_2_out, ~count_of_players[0], ~count_of_players[1]);  // AND_Gate
  not not_3 (not_3_out, and_2_out);
  not not_4 (not_4_out, not_3_out);
  and and_3 (and_3_out, not_3_out, not_4_out);
  S_R_Flip_Flop #(.trigger("low")) s_r_ff_1 (
    .S(and_3_out), .clk(1'b0), .R(and_1_out), .Q(input_players), .reset(reset_all));  // open: Qn, preset, en

  assign count_of_players[7:2] = {6{1'b0}};
endmodule
